# Fritzing sketch TekTreev1 (saved by Fritzing 0.9.2b)
breadboards: 1

parts:
  Part1 = Arduino Uno (Rev3) - ICSP
  LED2 = LED - 3mm [color="Red (633nm)" package="3 mm [THT]"]
  LED3 = LED - 3mm [color="Red (633nm)" package="3 mm [THT]"]
  LED4 = LED - 3mm [color="Red (633nm)" package="3 mm [THT]"]
  LED5 = LED - 3mm [color="Red (633nm)" package="3 mm [THT]"]
  LED6 = LED - 3mm [color="Red (633nm)" package="3 mm [THT]"]
  LED7 = LED - 3mm [color="Red (633nm)" package="3 mm [THT]"]
  LED8 = LED - 3mm [color="Red (633nm)" package="3 mm [THT]"]
  LED9 = LED - 3mm [color="Red (633nm)" package="3 mm [THT]"]
  LED10 = LED - 3mm [color="Red (633nm)" package="3 mm [THT]"]
  LED11 = LED - 3mm [color="Red (633nm)" package="3 mm [THT]"]
  S1 = Pushbutton [package="[THT]"]
  R1 = Rotary Potentiometer (Large) [maximum_resistance=100kΩ package=THT]
  R2 = Rotary Potentiometer (Large) [maximum_resistance=100kΩ package=THT]
  LED13 = LED - 3mm [color="Red (633nm)" package="3 mm [THT]"]
  LED14 = LED - 3mm [color="Red (633nm)" package="3 mm [THT]"]
  LED15 = LED - 3mm [color="Red (633nm)" package="3 mm [THT]"]
  LED16 = LED - 3mm [color="Red (633nm)" package="3 mm [THT]"]
  LED17 = LED - 3mm [color="Red (633nm)" package="3 mm [THT]"]
  R3 = Resistor [tolerance=±5% resistance=220 package=THT]

nets:
  N1: Part1.A0, R2.wiper
  N2: Part1.D8, LED3.anode
  N3: Part1.D9_PWM, LED2.anode
  N4: Part1.D10_PWM/SS, LED13.anode, LED14.anode, LED15.anode, LED16.anode, LED17.anode
  N5: Part1.D11_PWM/MOSI, S1.Pin_1, S1.Pin_2, R3.Pin_0
  N6: Part1.D0/RX, LED11.anode
  N7: Part1.D1/TX, LED10.anode
  N8: Part1.D2, LED9.anode
  N9: Part1.D3_PWM, LED8.anode
  N10: Part1.D4, LED7.anode
  N11: Part1.D5_PWM, LED6.anode
  N12: Part1.D6_PWM, LED5.anode
  N13: Part1.D7, LED4.anode
  N14: Part1.5V, S1.Pin_3, S1.Pin_4, R1.leg1, R2.leg1
  N15: Part1.GND, LED2.cathode, LED3.cathode, LED4.cathode, LED5.cathode, LED6.cathode, LED7.cathode, LED8.cathode, LED9.cathode, LED10.cathode, LED11.cathode, R1.leg2, R2.leg2, LED13.cathode, LED14.cathode, LED15.cathode, LED16.cathode, LED17.cathode, R3.Pin_1

notes:
  No idea what I'm going to use the 2nd pot for.
